// Logisim project CustomMultiplier.circ as structural Verilog: 2 circuits, main circuit CustomMultiplier
module CustomMultiplier (
  input  [7:0] FirstOperand,
  input  [7:0] SecondOperand,
  input  in_3,
  output [7:0] Result,
  output Done
);

  wire and_1_out, and_2_out, changechecker_1_out_3, changechecker_2_out_3, comparator_2_eq, nand_1_out,
       or_1_out;
  wire [7:0] counter_1_q, customadder_1_result, register_1_q;

  nand nand_1 (nand_1_out, ~or_1_out, Done);  // NAND_Gate
  and and_1 (and_1_out, in_3, nand_1_out);
  Counter counter_1 (
    .load(or_1_out), .up(1'b0), .clk(and_1_out), .D(SecondOperand), .Q(counter_1_q));  // open: clr, count, carry
  ChangeChecker changechecker_1 (.in_1(FirstOperand), .clk(in_3), .out_3(changechecker_1_out_3));
  or or_1 (or_1_out, changechecker_1_out_3, changechecker_2_out_3);
  ChangeChecker changechecker_2 (.in_1(SecondOperand), .clk(in_3), .out_3(changechecker_2_out_3));
  Register register_1 (.D(customadder_1_result), .clk(and_2_out), .Q(register_1_q), .clr(or_1_out));  // open: en
  CustomAdder customadder_1 (.FirstOperand(register_1_q), .SecondOperand(FirstOperand), .Result(customadder_1_result));
  and and_2 (and_2_out, in_3, ~Done);  // AND_Gate
  Comparator comparator_1 (.a({8{1'b0}}), .b(counter_1_q), .eq(Done));  // open: gt, lt
  Comparator comparator_2 (.a({8{1'b0}}), .b(SecondOperand), .eq(comparator_2_eq));  // open: gt, lt
  Multiplexer #(.width(8)) multiplexer_1 (.in0(register_1_q), .in1({8{1'b0}}), .out(Result), .sel(comparator_2_eq));
endmodule

module ChangeChecker (
  input  [7:0] in_1,
  input  clk,
  output out_3
);

  wire comparator_1_gt, comparator_1_lt;
  wire [7:0] register_1_q;

  Register register_1 (.D(in_1), .clk(clk), .Q(register_1_q));  // open: en, clr
  Comparator comparator_1 (.a(in_1), .b(register_1_q), .gt(comparator_1_gt), .lt(comparator_1_lt));  // open: eq
  or or_1 (out_3, comparator_1_gt, comparator_1_lt);
endmodule
